// Logisim project CPU.circ as structural Verilog: 1 circuit, main circuit DMEM
module DMEM (
  input  [15:0] ADDRESS,
  input  MemWrite,
  input  MemRead,
  input  Clear,
  input  WORD_EN,
  input  [15:0] DATA_IN,
  input  ENDIANNESS,
  output [15:0] DATA_OUT
);

  wire clock_1_out, multiplexer_6_out, not_1_out, or_1_out, or_2_out;
  wire [7:0] multiplexer_1_out, multiplexer_2_out, multiplexer_3_out, multiplexer_4_out, ram_1_data,
       ram_2_data;

  Clock clock_1 (.out(clock_1_out));
  Multiplexer #(.width(8), .enable("false")) multiplexer_1 (
    .in0(DATA_IN[7:0]), .in1(DATA_IN[15:8]), .out(multiplexer_1_out), .sel(multiplexer_6_out));
  Multiplexer #(.width(8), .enable("false")) multiplexer_2 (
    .in0(DATA_IN[15:8]), .in1(DATA_IN[7:0]), .out(multiplexer_2_out), .sel(multiplexer_6_out));
  or or_1 (or_1_out, not_1_out, WORD_EN);
  not not_1 (not_1_out, ADDRESS[0]);
  or or_2 (or_2_out, ADDRESS[0], WORD_EN);
  RAM #(.addrWidth(15), .bus("separate")) ram_1 (
    .addr(ADDRESS[15:1]), .din(multiplexer_1_out), .data(ram_1_data), .str(MemWrite), .sel(or_1_out),
    .clk(clock_1_out), .ld(MemRead), .clr(Clear));
  RAM #(.addrWidth(15), .bus("separate")) ram_2 (
    .addr(ADDRESS[15:1]), .din(multiplexer_2_out), .data(ram_2_data), .str(MemWrite), .sel(or_2_out),
    .clk(clock_1_out), .ld(MemRead), .clr(Clear));
  Multiplexer #(.width(8), .enable("false")) multiplexer_3 (
    .in0({8{1'b0}}), .in1(ram_1_data), .out(multiplexer_3_out), .sel(or_1_out));
  Multiplexer #(.width(8), .enable("false")) multiplexer_4 (
    .in0({8{1'b0}}), .in1(ram_2_data), .out(multiplexer_4_out), .sel(or_2_out));
  Multiplexer #(.width(16), .enable("false")) multiplexer_5 (
    .in0({multiplexer_4_out, multiplexer_3_out}), .in1({multiplexer_3_out, multiplexer_4_out}),
    .out(DATA_OUT), .sel(multiplexer_6_out));
  Multiplexer #(.enable("false")) multiplexer_6 (
    .in0(ADDRESS[0]), .in1(ENDIANNESS), .out(multiplexer_6_out), .sel(WORD_EN));
endmodule
